// Logisim project aritmetica.circ as structural Verilog: 1 circuit, main circuit main
module main (
  input  [1:0] S1_S0,
  input  Cin,
  input  [15:0] A,
  input  [15:0] B,
  output [15:0] \saída ,
  output Overflow,
  output Negative,
  output Cout
);

  wire adder_1_cout;
  wire [15:0] and_1_out, and_2_out, not_1_out, or_1_out;

  assign and_1_out = {16{S1_S0[0]}} & A;  // AND_Gate and_1, 16 bits wide
  assign and_2_out = {16{S1_S0[1]}} & not_1_out;  // AND_Gate and_2, 16 bits wide
  assign not_1_out = ~A;  // NOT_Gate not_1, 16 bits wide
  assign or_1_out = and_1_out | and_2_out;  // OR_Gate or_1, 16 bits wide
  Adder #(.width(15)) adder_1 (.a(B[14:0]), .b(or_1_out[14:0]), .out(\saída [14:0]), .cin(Cin), .cout(adder_1_cout));
  Adder #(.width(1)) adder_2 (.a(B[15]), .b(or_1_out[15]), .out(Negative), .cin(adder_1_cout), .cout(Cout));
  xor xor_1 (Overflow, adder_1_cout, Cout);

  assign \saída [15] = Negative;
endmodule
