// Logisim project branch-control.circ as structural Verilog: 1 circuit, main circuit main
module main (
  input  PL,
  input  JB,
  input  BC,
  input  N,
  input  Z,
  output OUT,
  output PS
);

  wire and_1_out, and_2_out, and_4_out, and_5_out, not_1_out, not_2_out, not_3_out, not_4_out, or_1_out;

  not not_1 (not_1_out, BC);
  and and_1 (and_1_out, PL, not_2_out, not_3_out);
  not not_2 (not_2_out, JB);
  not not_3 (not_3_out, BC);
  not not_4 (not_4_out, JB);
  and and_2 (and_2_out, PL, not_4_out, BC);
  and and_3 (PS, PL, JB, or_1_out);
  or or_1 (or_1_out, BC, not_1_out);
  and and_4 (and_4_out, Z, and_1_out);
  and and_5 (and_5_out, N, and_2_out);
  or or_2 (OUT, and_4_out, and_5_out, PS);
endmodule
