// Logisim project function-unit.circ as structural Verilog: 1 circuit, main circuit main
module main (
  input  [15:0] A,
  input  [15:0] B,
  input  [3:0] S2_S1_S0_cin,
  output OVF,
  output NEG,
  output COUT,
  output Z,
  output [15:0] OUT
);

  wire and_1_out;
  wire [15:0] Shifter_out_3, ULA_g;

  barrel_shifter_main Shifter (.in_1(B), .S1_S0(S2_S1_S0_cin[1:0]), .out_3(Shifter_out_3));
  and and_1 (and_1_out, S2_S1_S0_cin[2], S2_S1_S0_cin[3]);
  ula_completa_main ULA (.S2_S1_Cin(S2_S1_S0_cin), .A(A), .B(B), .OVF(OVF), .NEG(NEG), .COUT(COUT), .G(ULA_g));
  zero_fill_main main_1 (.IN(ULA_g), .out_2(Z));
  Multiplexer #(.width(16)) multiplexer_1 (.in0(ULA_g), .in1(Shifter_out_3), .out(OUT), .sel(and_1_out));  // open: en
endmodule
