// Logisim project palavra-de-controle.circ as structural Verilog: 1 circuit, main circuit main
module main (
  input  [15:0] Instruction,
  output [2:0] DA,
  output [2:0] AA,
  output [2:0] BA,
  output MB,
  output [3:0] FS,
  output MD,
  output RW,
  output MW,
  output PL,
  output JB,
  output BC
);

  wire not_1_out, not_3_out;

  not not_1 (not_1_out, PL);
  and and_1 (FS[0], Instruction[9], not_1_out);
  not not_2 (RW, Instruction[14]);
  not not_3 (not_3_out, Instruction[15]);
  and and_2 (PL, Instruction[14], Instruction[15]);
  and and_3 (MW, Instruction[14], not_3_out);

  assign AA = Instruction[5:3];
  assign BA = Instruction[2:0];
  assign BC = Instruction[9];
  assign DA = Instruction[8:6];
  assign FS[3:1] = Instruction[12:10];
  assign JB = Instruction[13];
  assign MB = Instruction[15];
  assign MD = Instruction[13];
endmodule
