// Logisim project pc.circ as structural Verilog: 1 circuit, main circuit main
module main (
  input  [2:0] IR_0_2,
  input  Load,
  input  [1:0] IR_7_6,
  input  _8,
  input  Clk,
  input  Reset,
  input  [15:0] BUSA,
  input  PS,
  output [15:0] \Saída_InstructionAdress 
);

  wire not_1_out;
  wire [15:0] adder_1_out, bit_extender_1_out, bit_extender_2_out, multiplexer_1_out, multiplexer_2_out,
       multiplexer_3_out;

  assign bit_extender_1_out = {{11{1'b0}}, {IR_7_6, IR_0_2}};  // Bit_Extender bit_extender_1
  assign bit_extender_2_out = {{11{1'b1}}, {IR_7_6, IR_0_2}};  // Bit_Extender bit_extender_2
  Multiplexer #(.width(16)) multiplexer_1 (
    .in0(bit_extender_1_out), .in1(bit_extender_2_out), .out(multiplexer_1_out), .sel(_8));  // open: en
  Multiplexer #(.width(16)) multiplexer_2 (
    .in0(multiplexer_1_out), .in1(BUSA), .out(multiplexer_2_out), .sel(PS));  // open: en
  Adder #(.width(16)) adder_1 (
    .a(\Saída_InstructionAdress ), .b(multiplexer_2_out), .out(adder_1_out));  // open: cin, cout
  not not_1 (not_1_out, Load);
  Multiplexer #(.width(16)) multiplexer_3 (
    .in0(adder_1_out), .in1(multiplexer_2_out), .out(multiplexer_3_out), .sel(PS));  // open: en
  Counter #(.width(16), .max('hffff)) counter_1 (
    .load(Load), .D(multiplexer_3_out), .count(not_1_out), .Q(\Saída_InstructionAdress ), .clk(Clk),
    .clr(Reset));  // open: carry
endmodule
