// Logisim project processador.circ as structural Verilog: 1 circuit, main circuit main
module main (
  input  in_1,
  output [15:0] out_2
);

  wire BC, C, CLK, JB, MB, MD, MW, N, OUT, PL, PS, RW, V, Z;
  wire [1:0] rom_1_data_2;
  wire [2:0] AA, BA, DA, IR;
  wire [3:0] FS;
  wire [15:0] bit_extender_1_out, BUSA, BUSB, Data_In, Data_in_t, \main_1_saída_instructionadress ;
  wire [15:3] rom_1_data;

  Clock clock_1 (.out(CLK));
  pc_main main_1 (
    ._8(rom_1_data[8]), .IR_7_6(rom_1_data_2), .IR_0_2(IR),
    .\Saída_InstructionAdress (\main_1_saída_instructionadress ), .Load(OUT), .BUSA(BUSA), .PS(PS),
    .Clk(CLK), .Reset(in_1));
  branch_control_main Branch_Control (.PL(PL), .JB(JB), .BC(BC), .N(N), .Z(Z), .OUT(OUT), .PS(PS));
  assign bit_extender_1_out = {{13{1'b0}}, IR};  // Bit_Extender bit_extender_1
  ROM #(.addrWidth(16), .dataWidth(16)) rom_1 (
    .addr(\main_1_saída_instructionadress ), .data({rom_1_data[15:8], rom_1_data_2, rom_1_data[5:3], IR}));  // open: sel
  palavra_de_controle_main main_2 (
    .Instruction({rom_1_data[15:8], rom_1_data_2, rom_1_data[5:3], IR}), .DA(DA), .AA(AA), .BA(BA), .MB(MB),
    .FS(FS), .MD(MD), .RW(RW), .MW(MW), .PL(PL), .JB(JB), .BC(BC));
  data_path_main main_3 (
    .Constant_In(bit_extender_1_out), .MB_Select(MB), .Data_In(Data_In), .Clk(CLK), .S2_S1_S0_Cin(FS),
    .BUS_A__ULA_A(BUSA), .OUT(out_2), .BUS_B__ULA_B(BUSB), .out_14(V), .out_15(N), .out_16(C), .out_17(Z),
    .Load_Enable(RW), .A_Select(AA), .B_Select(BA), .Destination_Select(DA), .MD(MD));
  RAM #(.addrWidth(16), .dataWidth(16), .bus("separate")) ram_1 (
    .addr(BUSA), .din(BUSB), .data(Data_in_t), .str(MW), .clk(CLK), .ld(1'b1));  // open: sel, clr

  // Notes on the sheet:
  //   contents of rom_1 (hex, n*v repeats v):
  //   9803 9842 9881 98c2 9903 9942 9981 99c2 204 200 408 e000
endmodule
