// Logisim project ula-completa.circ as structural Verilog: 1 circuit, main circuit main
module main (
  input  [3:0] S2_S1_Cin,
  input  [15:0] A,
  input  [15:0] B,
  output OVF,
  output NEG,
  output COUT,
  output [15:0] G
);

  wire [15:0] \main_1_saída , main_2_out_4;

  aritmetica_main main_1 (
    .S1_S0(S2_S1_Cin[2:1]), .Cin(S2_S1_Cin[0]), .A(A), .B(B), .\saída (\main_1_saída ), .Overflow(OVF),
    .Negative(NEG), .Cout(COUT));
  logica_main main_2 (.in_1(A), .in_2(B), .out_4(main_2_out_4), .S1_S0(S2_S1_Cin[1:0]));
  Multiplexer #(.width(16)) multiplexer_1 (
    .in0(\main_1_saída ), .in1(main_2_out_4), .out(G), .sel(S2_S1_Cin[3]));  // open: en
endmodule
